// Logisim project CPU.circ as structural Verilog: 9 circuits, main circuit main
module main (
  input  [31:0] in_1,
  input  [31:0] A,
  input  [31:0] B
);

  wire CLK, reset;
  wire [2:0] alu_1_flag_out_70c782f8;
  wire [12:0] controlunit_1_alusignals;
  wire [31:0] alu_1_dout;

  Clock clock_1 (.out(CLK));
  Clock clock_2 (.out(reset));
  ControlUnit controlunit_1 (
    .Instruction(in_1), .AluSignals(controlunit_1_alusignals));  // open: IsImmediate, IsLd, IsSt, IsBeq, IsBgt, IsCall, IsRet, IsWb, IsUbranch
  IFetch ifetch_1 (.CLK(CLK), .reset(reset));  // open: IsBranchTaken, BranchPC, Instruction
  oFetch ofetch_1 ();  // open: PC, isSt, isRet, Immx
  // Probe on alu_1_dout
  ALU alu_1 (
    .Instruction(controlunit_1_alusignals), .Reg_A_7969c0f7(A), .Reg_B_c40337f3(B), .Dout(alu_1_dout),
    .Flag_out_70c782f8(alu_1_flag_out_70c782f8));
  // Probe on alu_1_flag_out_70c782f8
endmodule

module IFetch (
  input  IsBranchTaken,
  input  [31:0] BranchPC,
  input  CLK,
  input  reset,
  output [31:0] Instruction
);

  wire undriven;
  wire [31:0] adder_1_out, multiplexer_1_out, PC_q;

  Register #(.trigger("falling"), .width(32)) PC (.D(multiplexer_1_out), .en(1'b1), .clk(CLK), .Q(PC_q), .clr(reset));
  Multiplexer #(.width(32)) multiplexer_1 (.in0(adder_1_out), .in1(BranchPC), .out(multiplexer_1_out), .sel(undriven));
  Adder #(.width(32)) adder_1 (.a(32'h4), .b(PC_q), .out(adder_1_out));  // open: cin, cout
  ROM #(.addrWidth(16), .dataWidth(32)) Instruction_Memory_0469d480 (.addr(PC_q[31:16]), .data(Instruction));

  // Other names for the same wires on the sheet: clock = CLK

  // Notes on the sheet:
  //   contents of Instruction_Memory_0469d480 (hex, n*v repeats v):
  //   4c00000a 98000002 90000000 2c000001 88000003 4c400001 a0000000 fb80008 7c380000 7ff80004 c000001
  //   9ffffff8 77f80004 74380000 7b80008 10404000 a0000000
endmodule

module oFetch (
  input  [31:0] PC,
  input  isSt,
  input  isRet,
  output [31:0] Immx
);

  wire [3:0] A1, A2;
  wire [26:0] Instruction;
  wire [31:0] bit_extender_1_out, bit_extender_2_out, bit_extender_3_out, BranchTarget, shifter_1_out,
       shifter_2_out;

  assign bit_extender_1_out = {{5{Instruction[26]}}, Instruction};  // Bit_Extender bit_extender_1
  assign bit_extender_2_out = {{16{Instruction[16]}}, Instruction[16:1]};  // Bit_Extender bit_extender_2
  assign bit_extender_3_out = {{16{1'b0}}, Instruction[16:1]};  // Bit_Extender bit_extender_3
  Shifter #(.width(32)) shifter_1 (.in(bit_extender_1_out), .\dist (5'b00010), .out(shifter_1_out));
  Adder #(.width(32)) adder_1 (.a(shifter_1_out), .b(PC), .out(BranchTarget));  // open: cin, cout
  Multiplexer #(.width(4)) multiplexer_1 (.in0(Instruction[21:18]), .in1(4'b1111), .out(A1), .sel(isRet));
  Multiplexer #(.width(4)) multiplexer_2 (.in0(Instruction[25:22]), .in1(Instruction[17:14]), .out(A2), .sel(isSt));
  Shifter #(.width(32)) shifter_2 (.in(bit_extender_3_out), .\dist (5'b10000), .out(shifter_2_out));
  Multiplexer #(.select(2), .width(32)) multiplexer_3 (
    .in0(bit_extender_2_out), .in1(bit_extender_3_out), .in2(shifter_2_out), .out(Immx),
    .sel(Instruction[18:17]));  // open: in3

  // Notes on the sheet:
  //   Register input 1
  //   Register input 2
endmodule

module Ex (
);

  wire and_1_out, and_2_out, BranchPC, BranchTarget, IsBeq, IsBgt, IsBranchTaken, IsRet, IsUbranch,
       nor_1_out, op1;
  wire [2:1] Flag_out_70c782f8;

  and and_1 (and_1_out, IsBeq, Flag_out_70c782f8[1]);
  nor nor_1 (nor_1_out, Flag_out_70c782f8[2], Flag_out_70c782f8[1]);
  Multiplexer multiplexer_1 (.in0(BranchTarget), .in1(op1), .out(BranchPC), .sel(IsRet));
  and and_2 (and_2_out, IsBgt, nor_1_out);
  or or_1 (IsBranchTaken, IsUbranch, and_1_out, and_2_out);

  // Notes on the sheet:
  //   Flag.E
  //   Flag.GT
endmodule

module RW (
  input  Reset,
  input  isCall,
  input  isWb,
  input  [3:0] rd,
  input  [3:0] Read1,
  input  [3:0] Read2,
  input  [31:0] aluResult,
  input  [31:0] PC,
  input  isLd,
  input  [31:0] ldResult,
  output [31:0] Op1,
  output [31:0] Op2
);

  wire CLK;
  wire [3:0] multiplexer_2_out;
  wire [31:0] adder_1_out, multiplexer_1_out;

  Clock clock_1 (.out(CLK));
  Adder #(.width(32)) adder_1 (.a(PC), .b(32'h4), .out(adder_1_out));  // open: cin, cout
  Multiplexer #(.select(2), .width(32)) multiplexer_1 (
    .in0(aluResult), .in1(ldResult), .in2(adder_1_out), .out(multiplexer_1_out), .sel({isCall, isLd}));  // open: in3
  Multiplexer #(.width(4)) multiplexer_2 (.in0(rd), .in1(4'b1111), .out(multiplexer_2_out), .sel(isCall));
  Register_File register_file_1 (
    .A1(Read1), .A2(Read2), .A(multiplexer_2_out), .D(multiplexer_1_out), .CLK(CLK), .Reset(Reset), .E(isWb),
    .D1(Op1), .D2(Op2));
endmodule

module ControlUnit (
  input  [31:0] Instruction,
  output IsImmediate,
  output [12:0] AluSignals,
  output IsLd,
  output IsSt,
  output IsBeq,
  output IsBgt,
  output IsCall,
  output IsRet,
  output IsWb,
  output IsUbranch
);

  wire and_1_out, and_2_out, and_3_out, and_4_out, demultiplexer_1_out0, demultiplexer_1_out18, nor_1_out,
       not_1_out, not_2_out, not_3_out, not_4_out, not_5_out, or_1_out, or_2_out;

  Demultiplexer #(.select(5)) demultiplexer_1 (
    .out0(demultiplexer_1_out0), .out1(AluSignals[1]), .out2(AluSignals[2]), .out3(AluSignals[3]),
    .out4(AluSignals[4]), .out5(AluSignals[5]), .out6(AluSignals[6]), .out7(AluSignals[7]),
    .out8(AluSignals[8]), .out9(AluSignals[9]), .out10(AluSignals[10]), .out11(AluSignals[11]),
    .out12(AluSignals[12]), .out14(IsLd), .out15(IsSt), .out16(IsBeq), .out17(IsBgt),
    .out18(demultiplexer_1_out18), .out19(IsCall), .out20(IsRet), .in(1'b1), .sel(Instruction[31:27]));  // open: out13, out21, out22, out23, out24, out25, out26, out27, out28, out29, out30, out31
  not not_1 (not_1_out, Instruction[27]);
  not not_2 (not_2_out, Instruction[28]);
  not not_3 (not_3_out, Instruction[29]);
  not not_4 (not_4_out, Instruction[30]);
  not not_5 (not_5_out, Instruction[31]);
  and and_1 (and_1_out, not_5_out, Instruction[30], Instruction[29], Instruction[28]);
  or or_1 (or_1_out, not_2_out, Instruction[30]);
  and and_2 (and_2_out, not_1_out, not_2_out, Instruction[29]);
  and and_3 (and_3_out, Instruction[28], not_3_out);
  or or_2 (or_2_out, and_2_out, and_3_out);
  or or_3 (AluSignals[0], demultiplexer_1_out0, and_1_out);
  and and_4 (and_4_out, Instruction[27], or_1_out, Instruction[29], not_5_out);
  nor nor_1 (nor_1_out, and_4_out, Instruction[31]);
  or or_4 (IsWb, IsCall, nor_1_out);
  and and_5 (IsUbranch, or_2_out, not_4_out, Instruction[31]);

  assign IsImmediate = Instruction[26];

  // Notes on the sheet:
  //   IsImmediate
  //   Is Add
  //   IsSub
  //   IsMul
  //   IsDiv
  //   IsMod
  //   IsCmp
  //   IsAnd
  //   IsOr
  //   IsNot
  //   IsMov
  //   IsLsl
  //   IsLsr
  //   IsAsr
  //   IsLd
  //   IsSt
  //   IsBeq
  //   IsBgt
  //   IsCall
  //   IsRet
  //   Is Add
  //   IsWb
  //   IsUbranch
endmodule

module ALU (
  input  [12:0] Instruction,
  input  [31:0] Reg_A_7969c0f7,
  input  [31:0] Reg_B_c40337f3,
  output [31:0] Dout,
  output [2:0] Flag_out_70c782f8
);

  wire adder_1_cout, comparator_1_eq, comparator_1_gt, comparator_1_lt, subtractor_1_bout;
  wire [3:0] Choose;
  wire [31:0] adder_1_out, and_1_out, divider_1_out, divider_1_rem, multiplier_1_out, not_1_out, or_1_out,
       shifter_1_out, shifter_2_out, shifter_3_out, subtractor_1_out;

  assign or_1_out = Reg_A_7969c0f7 | Reg_B_c40337f3;  // OR_Gate or_1, 32 bits wide
  assign not_1_out = ~Reg_A_7969c0f7;  // NOT_Gate not_1, 32 bits wide
  assign and_1_out = Reg_A_7969c0f7 & Reg_B_c40337f3;  // AND_Gate and_1, 32 bits wide
  Adder #(.width(32)) adder_1 (
    .a(Reg_A_7969c0f7), .b(Reg_B_c40337f3), .out(adder_1_out), .cout(adder_1_cout));  // open: cin
  assign Flag_out_70c782f8[0] = Instruction[0] ? adder_1_cout : 1'bz;  // Controlled_Buffer controlled_buffer_1
  Subtractor #(.width(32)) subtractor_1 (
    .a(Reg_A_7969c0f7), .b(Reg_B_c40337f3), .out(subtractor_1_out), .bout(subtractor_1_bout));  // open: bin
  assign Flag_out_70c782f8[2] = Instruction[1] ? subtractor_1_bout : 1'bz;  // Controlled_Buffer controlled_buffer_2
  assign Flag_out_70c782f8[0] = Instruction[5] ? comparator_1_gt : 1'bz;  // Controlled_Buffer controlled_buffer_3
  assign Flag_out_70c782f8[1] = Instruction[5] ? comparator_1_eq : 1'bz;  // Controlled_Buffer controlled_buffer_4
  Comparator #(.width(32)) comparator_1 (
    .a(Reg_A_7969c0f7), .b(Reg_B_c40337f3), .gt(comparator_1_gt), .eq(comparator_1_eq), .lt(comparator_1_lt));
  assign Flag_out_70c782f8[2] = Instruction[5] ? comparator_1_lt : 1'bz;  // Controlled_Buffer controlled_buffer_5
  Multiplier #(.width(32)) multiplier_1 (
    .a(Reg_A_7969c0f7), .b(Reg_B_c40337f3), .out(multiplier_1_out));  // open: cin, cout
  Divider #(.width(32)) divider_1 (
    .a(Reg_A_7969c0f7), .b(Reg_B_c40337f3), .out(divider_1_out), .rem(divider_1_rem));  // open: upper
  Shifter #(.width(32)) shifter_1 (.in(Reg_A_7969c0f7), .\dist (Reg_B_c40337f3[4:0]), .out(shifter_1_out));
  Shifter #(.shift("lr"), .width(32)) shifter_2 (
    .in(Reg_A_7969c0f7), .\dist (Reg_B_c40337f3[4:0]), .out(shifter_2_out));
  Shifter #(.shift("ar"), .width(32)) shifter_3 (
    .in(Reg_A_7969c0f7), .\dist (Reg_B_c40337f3[4:0]), .out(shifter_3_out));
  assign Choose = Instruction[0] ? 4'b0000 : 4'bz;  // Controlled_Buffer controlled_buffer_6
  assign Choose = Instruction[1] ? 4'b0001 : 4'bz;  // Controlled_Buffer controlled_buffer_7
  assign Choose = Instruction[5] ? 4'b0010 : 4'bz;  // Controlled_Buffer controlled_buffer_8
  assign Choose = Instruction[2] ? 4'b0011 : 4'bz;  // Controlled_Buffer controlled_buffer_9
  assign Choose = Instruction[3] ? 4'b0100 : 4'bz;  // Controlled_Buffer controlled_buffer_10
  assign Choose = Instruction[4] ? 4'b0101 : 4'bz;  // Controlled_Buffer controlled_buffer_11
  assign Choose = Instruction[10] ? 4'b0110 : 4'bz;  // Controlled_Buffer controlled_buffer_12
  assign Choose = Instruction[11] ? 4'b0111 : 4'bz;  // Controlled_Buffer controlled_buffer_13
  assign Choose = Instruction[12] ? 4'b1000 : 4'bz;  // Controlled_Buffer controlled_buffer_14
  assign Choose = Instruction[7] ? 4'b1001 : 4'bz;  // Controlled_Buffer controlled_buffer_15
  assign Choose = Instruction[8] ? 4'b1010 : 4'bz;  // Controlled_Buffer controlled_buffer_16
  assign Choose = Instruction[6] ? 4'b1011 : 4'bz;  // Controlled_Buffer controlled_buffer_17
  assign Choose = Instruction[9] ? 4'b1100 : 4'bz;  // Controlled_Buffer controlled_buffer_18
  Multiplexer #(.enable("true"), .select(4), .width(32)) multiplexer_1 (
    .in0(adder_1_out), .in1(subtractor_1_out), .in3(multiplier_1_out), .in4(divider_1_out),
    .in5(divider_1_rem), .in6(shifter_1_out), .in7(shifter_2_out), .in8(shifter_3_out), .in9(or_1_out),
    .in10(not_1_out), .in11(and_1_out), .in12(Reg_A_7969c0f7), .out(Dout), .sel(Choose), .en(1'b1));  // open: in2, in13, in14, in15
  // Probe on Choose
  assign Flag_out_70c782f8[1] = Instruction[0] ? 1'b0 : 1'bz;  // Controlled_Buffer controlled_buffer_19
  assign Flag_out_70c782f8[2] = Instruction[0] ? 1'b0 : 1'bz;  // Controlled_Buffer controlled_buffer_20
  assign Flag_out_70c782f8[0] = Instruction[1] ? 1'b0 : 1'bz;  // Controlled_Buffer controlled_buffer_21
  assign Flag_out_70c782f8[1] = Instruction[1] ? 1'b0 : 1'bz;  // Controlled_Buffer controlled_buffer_22
  assign Flag_out_70c782f8[1] = Instruction[7] ? 1'b0 : 1'bz;  // Controlled_Buffer controlled_buffer_23
  assign Flag_out_70c782f8[2] = Instruction[7] ? 1'b0 : 1'bz;  // Controlled_Buffer controlled_buffer_24
  assign Flag_out_70c782f8[0] = Instruction[7] ? 1'b0 : 1'bz;  // Controlled_Buffer controlled_buffer_25
  assign Flag_out_70c782f8[1] = Instruction[8] ? 1'b0 : 1'bz;  // Controlled_Buffer controlled_buffer_26
  assign Flag_out_70c782f8[2] = Instruction[8] ? 1'b0 : 1'bz;  // Controlled_Buffer controlled_buffer_27
  assign Flag_out_70c782f8[0] = Instruction[8] ? 1'b0 : 1'bz;  // Controlled_Buffer controlled_buffer_28
  assign Flag_out_70c782f8[1] = Instruction[2] ? 1'b0 : 1'bz;  // Controlled_Buffer controlled_buffer_29
  assign Flag_out_70c782f8[2] = Instruction[2] ? 1'b0 : 1'bz;  // Controlled_Buffer controlled_buffer_30
  assign Flag_out_70c782f8[0] = Instruction[2] ? 1'b0 : 1'bz;  // Controlled_Buffer controlled_buffer_31
  assign Flag_out_70c782f8[1] = Instruction[10] ? 1'b0 : 1'bz;  // Controlled_Buffer controlled_buffer_32
  assign Flag_out_70c782f8[2] = Instruction[10] ? 1'b0 : 1'bz;  // Controlled_Buffer controlled_buffer_33
  assign Flag_out_70c782f8[0] = Instruction[10] ? 1'b0 : 1'bz;  // Controlled_Buffer controlled_buffer_34
  assign Flag_out_70c782f8[1] = Instruction[11] ? 1'b0 : 1'bz;  // Controlled_Buffer controlled_buffer_35
  assign Flag_out_70c782f8[2] = Instruction[11] ? 1'b0 : 1'bz;  // Controlled_Buffer controlled_buffer_36
  assign Flag_out_70c782f8[0] = Instruction[11] ? 1'b0 : 1'bz;  // Controlled_Buffer controlled_buffer_37
  assign Flag_out_70c782f8[1] = Instruction[6] ? 1'b0 : 1'bz;  // Controlled_Buffer controlled_buffer_38
  assign Flag_out_70c782f8[2] = Instruction[6] ? 1'b0 : 1'bz;  // Controlled_Buffer controlled_buffer_39
  assign Flag_out_70c782f8[0] = Instruction[6] ? 1'b0 : 1'bz;  // Controlled_Buffer controlled_buffer_40
  assign Flag_out_70c782f8[1] = Instruction[4] ? 1'b0 : 1'bz;  // Controlled_Buffer controlled_buffer_41
  assign Flag_out_70c782f8[2] = Instruction[4] ? 1'b0 : 1'bz;  // Controlled_Buffer controlled_buffer_42
  assign Flag_out_70c782f8[0] = Instruction[4] ? 1'b0 : 1'bz;  // Controlled_Buffer controlled_buffer_43
  assign Flag_out_70c782f8[1] = Instruction[11] ? 1'b0 : 1'bz;  // Controlled_Buffer controlled_buffer_44
  assign Flag_out_70c782f8[2] = Instruction[11] ? 1'b0 : 1'bz;  // Controlled_Buffer controlled_buffer_45
  assign Flag_out_70c782f8[0] = Instruction[11] ? 1'b0 : 1'bz;  // Controlled_Buffer controlled_buffer_46
  assign Flag_out_70c782f8[1] = Instruction[12] ? 1'b0 : 1'bz;  // Controlled_Buffer controlled_buffer_47
  assign Flag_out_70c782f8[2] = Instruction[12] ? 1'b0 : 1'bz;  // Controlled_Buffer controlled_buffer_48
  assign Flag_out_70c782f8[0] = Instruction[12] ? 1'b0 : 1'bz;  // Controlled_Buffer controlled_buffer_49
  assign Flag_out_70c782f8[1] = Instruction[9] ? 1'b0 : 1'bz;  // Controlled_Buffer controlled_buffer_50
  assign Flag_out_70c782f8[2] = Instruction[9] ? 1'b0 : 1'bz;  // Controlled_Buffer controlled_buffer_51
  assign Flag_out_70c782f8[0] = Instruction[9] ? 1'b0 : 1'bz;  // Controlled_Buffer controlled_buffer_52

  // Other names for the same wires on the sheet: C = Flag_out_70c782f8[0]; Z = Flag_out_70c782f8[1];
  //   N = Flag_out_70c782f8[2]; add = Instruction[0]; sub = Instruction[1]; mul = Instruction[2];
  //   div = Instruction[3]; isMod = Instruction[4]; cmp = Instruction[5]; isAnd = Instruction[6];
  //   isOr = Instruction[7]; isNot = Instruction[8]; mov = Instruction[9]; Lsl = Instruction[10];
  //   Lsr = Instruction[11]; Asr = Instruction[12]
endmodule

module Register_File (
  input  CLK,
  input  Reset,
  input  E,
  input  [31:0] D,
  input  [3:0] A1,
  input  [3:0] A,
  input  [3:0] A2,
  output [31:0] D1,
  output [31:0] D2
);

  wire [31:0] demultiplexer_1_out0, demultiplexer_1_out1, demultiplexer_1_out2, demultiplexer_1_out3,
       demultiplexer_1_out4, demultiplexer_1_out5, demultiplexer_1_out6, demultiplexer_1_out7,
       demultiplexer_1_out8, demultiplexer_1_out9, demultiplexer_1_out10, demultiplexer_1_out11,
       demultiplexer_1_out12, demultiplexer_1_out13, demultiplexer_1_out14, demultiplexer_1_out15,
       register_1_q, register_2_q, register_3_q, register_4_q, register_5_q, register_6_q, register_7_q,
       register_8_q, register_9_q, register_10_q, register_11_q, register_12_q, register_13_q, register_14_q,
       register_15_q, register_16_q;

  Multiplexer #(.select(4), .width(32)) multiplexer_1 (
    .in0(register_1_q), .in1(register_2_q), .in2(register_3_q), .in3(register_4_q), .in4(register_5_q),
    .in5(register_6_q), .in6(register_7_q), .in7(register_8_q), .in8(register_9_q), .in9(register_10_q),
    .in10(register_11_q), .in11(register_12_q), .in12(register_13_q), .in13(register_14_q),
    .in14(register_15_q), .in15(register_16_q), .out(D1), .sel(A1));
  Multiplexer #(.select(4), .width(32)) multiplexer_2 (
    .in0(register_1_q), .in1(register_2_q), .in2(register_3_q), .in3(register_4_q), .in4(register_5_q),
    .in5(register_6_q), .in6(register_7_q), .in7(register_8_q), .in8(register_9_q), .in9(register_10_q),
    .in10(register_11_q), .in11(register_12_q), .in12(register_13_q), .in13(register_14_q),
    .in14(register_15_q), .in15(register_16_q), .out(D2), .sel(A2));
  Register #(.width(32)) register_1 (.D(demultiplexer_1_out0), .en(E), .clk(CLK), .Q(register_1_q), .clr(Reset));
  Register #(.width(32)) register_2 (.D(demultiplexer_1_out1), .en(E), .clk(CLK), .Q(register_2_q), .clr(Reset));
  Register #(.width(32)) register_3 (.D(demultiplexer_1_out2), .en(E), .clk(CLK), .Q(register_3_q), .clr(Reset));
  Register #(.width(32)) register_4 (.D(demultiplexer_1_out3), .en(E), .clk(CLK), .Q(register_4_q), .clr(Reset));
  Register #(.width(32)) register_5 (.D(demultiplexer_1_out4), .en(E), .clk(CLK), .Q(register_5_q), .clr(Reset));
  Register #(.width(32)) register_6 (.D(demultiplexer_1_out5), .en(E), .clk(CLK), .Q(register_6_q), .clr(Reset));
  Register #(.width(32)) register_7 (.D(demultiplexer_1_out6), .en(E), .clk(CLK), .Q(register_7_q), .clr(Reset));
  Register #(.width(32)) register_8 (.D(demultiplexer_1_out7), .en(E), .clk(CLK), .Q(register_8_q), .clr(Reset));
  Register #(.width(32)) register_9 (.D(demultiplexer_1_out8), .en(E), .clk(CLK), .Q(register_9_q), .clr(Reset));
  Register #(.width(32)) register_10 (.D(demultiplexer_1_out9), .en(E), .clk(CLK), .Q(register_10_q), .clr(Reset));
  Register #(.width(32)) register_11 (.D(demultiplexer_1_out10), .en(E), .clk(CLK), .Q(register_11_q), .clr(Reset));
  Register #(.width(32)) register_12 (.D(demultiplexer_1_out11), .en(E), .clk(CLK), .Q(register_12_q), .clr(Reset));
  Register #(.width(32)) register_13 (.D(demultiplexer_1_out12), .en(E), .clk(CLK), .Q(register_13_q), .clr(Reset));
  Register #(.width(32)) register_14 (.D(demultiplexer_1_out13), .en(E), .clk(CLK), .Q(register_14_q), .clr(Reset));
  Register #(.width(32)) register_15 (.D(demultiplexer_1_out14), .en(E), .clk(CLK), .Q(register_15_q), .clr(Reset));
  Register #(.width(32)) register_16 (.D(demultiplexer_1_out15), .en(E), .clk(CLK), .Q(register_16_q), .clr(Reset));
  Demultiplexer #(.select(4), .width(32)) demultiplexer_1 (
    .out0(demultiplexer_1_out0), .out1(demultiplexer_1_out1), .out2(demultiplexer_1_out2),
    .out3(demultiplexer_1_out3), .out4(demultiplexer_1_out4), .out5(demultiplexer_1_out5),
    .out6(demultiplexer_1_out6), .out7(demultiplexer_1_out7), .out8(demultiplexer_1_out8),
    .out9(demultiplexer_1_out9), .out10(demultiplexer_1_out10), .out11(demultiplexer_1_out11),
    .out12(demultiplexer_1_out12), .out13(demultiplexer_1_out13), .out14(demultiplexer_1_out14),
    .out15(demultiplexer_1_out15), .in(D), .sel(A));

  // Other names for the same wires on the sheet: WE = E
endmodule

module MA (
  input  isLd,
  input  isSt,
  input  CLK,
  input  [31:0] AluResult,
  input  [31:0] Op2,
  output [31:0] LdResult
);

  wire or_1_out;
  wire [15:0] register_1_q;
  wire [31:0] MDR_q;

  Register #(.width(16)) register_1 (.D(AluResult[15:0]), .en(or_1_out), .clk(CLK), .Q(register_1_q));  // open: clr
  or or_1 (or_1_out, isSt, isLd);
  Register #(.width(32)) MDR (.D(Op2), .en(isSt), .clk(CLK), .Q(MDR_q));  // open: clr
  RAM #(.addrWidth(16), .dataWidth(32)) ram_1 (
    .addr(register_1_q), .we(isSt), .oe(isLd), .clk(CLK), .din(MDR_q), .dout(LdResult));
endmodule
